# Fritzing sketch Diagrama_electronico (saved by Fritzing 0.9.3b)
breadboards: 1

parts:
  Argon1 = Particle Argon
  V1 = DC Power [voltage=5V]
  TB6600 = IC, SIP package, 12 pins [chip_label=TB6600]
  M1 = Stepper Motor - Bipolar
  M2 = Stepper Motor - Bipolar
  Motor_DC = Vibration Motor- ROB-08449 [package=vibe-motor-10mm]
  Driver_Relay_4_Canales = IC, SIP package, 18 pins [chip_label="Driver Relay"]
  Q1 = NPN-Transistor [package="TO92 [THT]"]
  Switch_de_Agua = SWITCH-SPST-2 [package=switch-spst-vertical]
  R1 = Resistor [tolerance=±5% resistance=10k package=THT]
  Servomotor_1 = IC, SIP package, 3 pins [chip_label=SG90]
  Servomotor_2 = IC, SIP package, 3 pins [chip_label=SG90]
  Servomotor_3 = IC, SIP package, 3 pins [chip_label=SG90]
  Servomotor_4 = IC, SIP package, 3 pins [chip_label=SG90]
  V2 = DC Power [voltage=12V]
  Q3 = NPN-Transistor [package="TO92 [THT]"]
  Bomba_de_Agua = Vibration Motor- ROB-08449 [package=vibe-motor-10mm]
  L298N_With_no_Jumper_Regulator = IC, SIP package, 8 pins [chip_label=L298N]
  R2 = Resistor [tolerance=±5% resistance=1k package=THT]
  R3 = Resistor [tolerance=±5% resistance=1k package=THT]
  SP1 = SPEAKER [package=pcb_mount_speaker]

nets:
  GND: Argon1.GND, V1.V-, TB6600.pin2, TB6600.pin8, TB6600.pin10, TB6600.pin12, Driver_Relay_4_Canales.pin1, Driver_Relay_4_Canales.pin2, Driver_Relay_4_Canales.pin3, Driver_Relay_4_Canales.pin4, Driver_Relay_4_Canales.pin5, Switch_de_Agua.P, Servomotor_1.pin3, Servomotor_2.pin3, Servomotor_3.pin3, Servomotor_4.pin3, V2.V-, Bomba_de_Agua.-, L298N_With_no_Jumper_Regulator.pin3, L298N_With_no_Jumper_Regulator.pin7, SP1.-
  N1: Argon1.MO, TB6600.pin7
  N2: Argon1.MI, TB6600.pin11
  N3: Argon1.RX, TB6600.pin9
  N4: Argon1.TX, R3.Pin_1
  N5: Argon1.SDA, Switch_de_Agua.O, R1.Pin_1
  N6: Argon1.SCL, R2.Pin_1
  N7: Argon1.D2, Servomotor_1.pin1
  N8: Argon1.D3, Servomotor_2.pin1
  N9: Argon1.D4, Servomotor_3.pin1
  N10: Argon1.D5, Servomotor_4.pin1
  N11: Argon1.D6, L298N_With_no_Jumper_Regulator.pin5
  N12: Argon1.D7, SP1.+
  N13: V1.V+, Servomotor_1.pin2, Servomotor_2.pin2, Servomotor_3.pin2, Servomotor_4.pin2, L298N_With_no_Jumper_Regulator.pin4, L298N_With_no_Jumper_Regulator.pin6, L298N_With_no_Jumper_Regulator.pin8
  N14: TB6600.pin1, V2.V+, Q3.C
  N15: TB6600.pin3, Driver_Relay_4_Canales.pin17
  N16: TB6600.pin4, Driver_Relay_4_Canales.pin14
  N17: TB6600.pin5, Driver_Relay_4_Canales.pin11
  N18: TB6600.pin6, Driver_Relay_4_Canales.pin8
  N19: M1.A, Driver_Relay_4_Canales.pin18
  N20: M1.C, Driver_Relay_4_Canales.pin15
  N21: M1.B, Driver_Relay_4_Canales.pin12
  N22: M1.D, Driver_Relay_4_Canales.pin9
  N23: M2.A, Driver_Relay_4_Canales.pin16
  N24: M2.C, Driver_Relay_4_Canales.pin13
  N25: M2.B, Driver_Relay_4_Canales.pin10
  N26: M2.D, Driver_Relay_4_Canales.pin7
  N27: Motor_DC.+, L298N_With_no_Jumper_Regulator.pin2
  N28: Motor_DC.-, L298N_With_no_Jumper_Regulator.pin1
  N29: Driver_Relay_4_Canales.pin6, Q1.E
  N30: Q1.B, R3.Pin_0
  N31: Q1.C, R1.Pin_0
  N32: Q3.E, Bomba_de_Agua.+
  N33: Q3.B, R2.Pin_0

custom parts:
  Particle Argon: The Argon is a powerful Wi-Fi enabled development board that can act as either a standalone Wi-Fi endpoint or Wi-Fi enabled gateway for Particle Mesh networks. It is based on the Nordic nRF52840 and has built-in battery charging circuitry so it’s easy to connect a Li-Po and deploy your local network in minutes. The Argon is great for connecting existing projects to the Particle Device Cloud or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
